# Fritzing sketch huntersattemptatfritzing (saved by Fritzing 0.9.3b)

parts:
  ZS-042_RTC1 = ZS-042 RTC Module
  Part1 = InvenSense MPU6050
  Part2 = OLED Monochrome 128x64 0.96 inch [part_number=326]
  MCU1 = Raspberry Pi Zero
  Part3 = Adafruit Micro USB Breakout [part_number="Adafruit #1833"]
  Part4 = Adafruit TCA9548A
  M1 = RioRand LM2596
  U1 = Mini-360 DC-DC Buck converter [package=THT]
  BAT1 = 18650 battery holder [package=battery-18650-kit]  # not connected
  BAT2 = 18650 battery holder [package=battery-18650-kit]  # not connected
  BUTTON1 = Waterproof Pushbutton (red)

nets:
  GND: ZS-042_RTC1.GND, Part1.GND, Part2.GND, MCU1.pin_6, MCU1.pin_8, MCU1.pin_9, Part4.GND, U1.OUT-, BUTTON1.no_name_yet#5
  VCC: ZS-042_RTC1.VCC, Part1.VCC, Part1.AD0, Part2.VIN, MCU1.pin_2, MCU1.pin_4, Part4.VCC, BUTTON1.no_name_yet#2, BUTTON1.no_name_yet#4
  N1: ZS-042_RTC1.SDA, Part1.SDA, MCU1.pin_3, Part4.INPUTSDA
  N2: ZS-042_RTC1.SCL, Part1.SCL, MCU1.pin_1, MCU1.pin_5, MCU1.pin_7, Part4.INPUTSCL
  N3: Part2.MOSI_SDA, Part4.0SDA
  N4: Part2.SCLK_SCK, Part4.0SCL
  N5: Part3.GND, M1.Pin_2
  N6: Part3.VBUS, M1.Pin_1
  N7: M1.Pin_3, U1.IN+
  N8: M1.Pin_4, U1.IN-
  N9: U1.OUT+, BUTTON1.no_name_yet#1

custom parts:
  OLED Monochrome 128x64 0.96 inch: These displays are small, only about 1" diameter, but very readable due to the high contrast of an OLED display. This display is made of 128x64 individual white OLED pixels, each one is turned on or off by the controller chip. Because the display makes its own light, no backlight is required. This reduces the power required to run the OLED and is why the display has such high contrast; we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
  Adafruit Micro USB Breakout: Simple but effective - this breakout board has a USB Micro-B connector, with all 5 pins broken out. Great for pairing with a microcontroller with USB support, or adding USB 5V power to a project. We use a micro-AB connector with through-hole shielding pads for an excellent strong connection - it won't rip off by accident! Comes with one fully assembled and tested micro B breakout PCB and a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
  Adafruit TCA9548A: You just found the perfect I2C sensor, and you want to wire up two or three or more of them to your Arduino when you realize "Uh oh, this chip has a fixed I2C address, and from what I know about I2C, you cannot have two devices with the same address on the same SDA/SCL pins!" Are you out of luck? You would be, if you didn't have this ultra-cool TCA9548A 1-to-8 I2C multiplexer! Finally, a way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
  Mini-360 DC-DC Buck converter: Mini-360 DC-DC Buck converter. Tiny buck step down voltage converter, input voltage 4.75 to 23V output 1 to 17V adjustable. Available from ebay and the like.
  18650 battery holder: 18650 Battery Holder
  Waterproof Pushbutton (red): Waterproof Illuminated Pushbutton (red)
